// Digital circuit batalha_naval.dig as structural Verilog
module batalha_naval (
  input  [3:0] in_1,
  input  [9:0] in_2,
  output [7:0] out_3,
  output [9:0] out_4,
  output [6:0] out_5,
  output [6:0] out_6,
  output [6:0] out_7,
  output [6:0] out_8,
  output [2:0] out_9,
  output [3:0] out_10,
  output [3:0] out_11,
  output [3:0] out_12,
  output [3:0] out_13
);

  batalha_naval #(.applicationType("GHDL"), .CodeFile("/home/piva/UFFS/Sistemas/TrabalhoFinal/batalha_naval.vhd")) u_batalha_naval (
    .key(in_1), .sw(in_2), .ledG(out_3), .ledR(out_4), .hex1(out_5), .hex2(out_6), .hex3(out_7),
    .hex4(out_8), .q_out(out_9), .o_barco1(out_10), .o_barco2_1(out_11), .o_barco2_2(out_12), .o_tiro(out_13));
endmodule
